# Fritzing sketch beerPong (saved by Fritzing 0.9.3b)
breadboards: 2

parts:
  Composant1 = Arduino Mega 2560 (Rev3)
  Composant7 = 24 NeoPixel Ring [part_number=1586]  # not connected
  J8 = Generic male header - 4 pins [form="♂ (male)" package=THT]
  Composant8 = 24 NeoPixel Ring [part_number=1586]  # not connected
  J9 = Generic male header - 4 pins [form="♂ (male)" package=THT]
  Composant9 = 24 NeoPixel Ring [part_number=1586]  # not connected
  J10 = Generic male header - 4 pins [form="♂ (male)" package=THT]
  Composant10 = 24 NeoPixel Ring [part_number=1586]  # not connected
  J11 = Generic male header - 4 pins [form="♂ (male)" package=THT]
  Composant11 = 24 NeoPixel Ring [part_number=1586]  # not connected
  J12 = Generic male header - 4 pins [form="♂ (male)" package=THT]
  Composant12 = 24 NeoPixel Ring [part_number=1586]  # not connected
  J13 = Generic male header - 4 pins [form="♂ (male)" package=THT]
  Composant13 = 24 NeoPixel Ring [part_number=1586]  # not connected
  J14 = Generic male header - 4 pins [form="♂ (male)" package=THT]
  Composant14 = 24 NeoPixel Ring [part_number=1586]  # not connected
  J15 = Generic male header - 4 pins [form="♂ (male)" package=THT]
  Composant15 = 24 NeoPixel Ring [part_number=1586]  # not connected
  J16 = Generic male header - 4 pins [form="♂ (male)" package=THT]
  Composant16 = 24 NeoPixel Ring [part_number=1586]  # not connected
  J17 = Generic male header - 4 pins [form="♂ (male)" package=THT]
  J19 = Generic male header - 2 pins [form="♂ (male)" package=THT]
  J20 = Generic male header - 2 pins [form="♂ (male)" package=THT]
  J21 = Generic male header - 2 pins [form="♂ (male)" package=THT]
  J22 = Generic male header - 2 pins [form="♂ (male)" package=THT]
  J23 = Generic male header - 2 pins [form="♂ (male)" package=THT]
  J24 = Generic male header - 2 pins [form="♂ (male)" package=THT]
  J25 = Generic male header - 2 pins [form="♂ (male)" package=THT]
  J26 = Generic male header - 2 pins [form="♂ (male)" package=THT]
  J27 = Generic male header - 2 pins [form="♂ (male)" package=THT]
  PIR1 = PIR sensor
  J28 = Generic male header - 3 pins [form="♀ (female)" package=THT]
  PIR2 = PIR sensor
  J29 = Generic male header - 3 pins [form="♀ (female)" package=THT]
  PIR3 = PIR sensor
  J30 = Generic male header - 3 pins [form="♀ (female)" package=THT]
  PIR4 = PIR sensor
  J31 = Generic male header - 3 pins [form="♀ (female)" package=THT]
  PIR5 = PIR sensor
  J32 = Generic male header - 3 pins [form="♀ (female)" package=THT]
  PIR6 = PIR sensor
  J33 = Generic male header - 3 pins [form="♀ (female)" package=THT]
  PIR7 = PIR sensor
  J34 = Generic male header - 3 pins [form="♀ (female)" package=THT]
  PIR8 = PIR sensor
  J35 = Generic male header - 3 pins [form="♀ (female)" package=THT]
  PIR9 = PIR sensor
  J36 = Generic male header - 3 pins [form="♀ (female)" package=THT]
  PIR10 = PIR sensor
  BUTTON1 = Waterproof Pushbutton (green)
  VCC1 = Battery
  C2 = Electrolytic Capacitor [capacitance=0.1µF package="0807 [SMD, electrolytic]"]
  U2 = Voltage Regulator - 5V [package="DPak [SMD]"]
  C3 = Electrolytic Capacitor [package="0807 [SMD, electrolytic]"]
  R1 = Resistor [tolerance=±5% resistance=10k package=THT]
  R11 = Photocell (LDR) [package=THT]
  R12 = Resistor [tolerance=±5% resistance=10k package=THT]
  R13 = Photocell (LDR) [package=THT]
  R14 = Resistor [tolerance=±5% resistance=10k package=THT]
  R15 = Resistor [tolerance=±5% resistance=10k package=THT]
  R16 = Photocell (LDR) [package=THT]
  R17 = Photocell (LDR) [package=THT]
  R18 = Resistor [tolerance=±5% resistance=10k package=THT]
  R19 = Resistor [tolerance=±5% resistance=10k package=THT]
  R20 = Resistor [tolerance=±5% resistance=10k package=THT]
  R21 = Resistor [tolerance=±5% resistance=10k package=THT]
  R22 = Photocell (LDR) [package=THT]
  R23 = Photocell (LDR) [package=THT]
  R24 = Photocell (LDR) [package=THT]
  R25 = Photocell (LDR) [package=THT]
  R26 = Resistor [tolerance=±5% resistance=10k package=THT]
  R27 = Resistor [tolerance=±5% resistance=10k package=THT]
  R28 = Photocell (LDR) [package=THT]
  R29 = Photocell (LDR) [package=THT]
  R30 = Resistor [tolerance=±5% resistance=10k package=THT]
  R31 = Resistor [tolerance=±5% resistance=10k package=THT]
  R32 = Resistor [tolerance=±5% resistance=10k package=THT]
  R33 = Resistor [tolerance=±5% resistance=10k package=THT]
  R34 = Resistor [tolerance=±5% resistance=10k package=THT]
  R35 = Resistor [tolerance=±5% resistance=10k package=THT]
  R36 = Resistor [tolerance=±5% resistance=10k package=THT]
  R37 = Resistor [tolerance=±5% resistance=10k package=THT]
  R38 = Resistor [tolerance=±5% resistance=10k package=THT]
  R40 = Resistor [tolerance=±5% resistance=10k package=THT]

nets:
  N1: Composant1.A8, R19.Pin_0, R23.pin_1
  N2: Composant1.A9, R27.Pin_0, R29.pin_1
  N3: Composant1.A10, R26.Pin_0, R28.pin_1
  N4: Composant1.A1, R1.Pin_0, R11.pin_1
  N5: Composant1.A2, R12.Pin_0, R13.pin_1
  N6: Composant1.A3, R14.Pin_0, R16.pin_1
  N7: Composant1.A4, R15.Pin_0, R17.pin_1
  N8: Composant1.A5, R18.Pin_0, R22.pin_1
  N9: Composant1.A6, R20.Pin_0, R25.pin_1
  N10: Composant1.A7, R21.Pin_0, R24.pin_1
  GND: Composant1.GND, J19.GND, BUTTON1.no_name_yet#5, VCC1.-, C2.+, U2.GND, C3.+, R1.Pin_1, R12.Pin_1, R14.Pin_1, R15.Pin_1, R18.Pin_1, R19.Pin_1, R20.Pin_1, R21.Pin_1, R30.Pin_1, R31.Pin_1, R34.Pin_1, R35.Pin_1, R36.Pin_1, R37.Pin_1, R38.Pin_1
  N11: Composant1.D11_PWM, J17.DI
  N12: Composant1.D10_PWM, J16.DI
  N13: Composant1.D9_PWM, J15.DI
  N14: Composant1.D8_PWM, J14.DI
  N15: Composant1.D2_PWM, J11.DI
  N16: Composant1.D3_PWM, J10.DI
  N17: Composant1.D4_PWM, J9.DI
  N18: Composant1.D5_PWM, J8.DI
  N19: Composant1.D6_PWM, J12.DI
  N20: Composant1.D7_PWM, J13.DI
  N21: Composant1.D22, PIR1.SIG
  N22: Composant1.D24, PIR2.SIG
  N23: Composant1.D26, PIR3.SIG
  N24: Composant1.D28, PIR4.SIG
  N25: Composant1.D30, PIR5.SIG
  N26: Composant1.D32, PIR6.SIG
  N27: Composant1.D34, PIR7.SIG
  N28: Composant1.D36, PIR8.SIG
  N29: Composant1.D38, PIR9.SIG
  N30: Composant1.D40, PIR10.SIG
  5V: J8.5V, J25.5V
  GND_2: J8.GND, J25.GND
  5V_2: J9.5V, J22.5V
  GND_3: J9.GND, J22.GND
  5V_3: J10.5V, J21.5V
  GND_4: J10.GND, J21.GND
  5V_4: J11.5V, J20.5V
  GND_5: J11.GND, J20.GND
  5V_5: J12.5V, J26.5V
  GND_6: J12.GND, J26.GND
  5V_6: J13.5V, J23.5V
  GND_7: J13.GND, J23.GND
  5V_7: J14.5V, J24.5V
  GND_8: J14.GND, J24.GND
  5V_8: J15.5V, J27.5V
  GND_9: J15.GND, J27.GND
  5V_9: J16.5V, J17.5V
  GND_10: J16.GND, J17.GND
  5V_10: J19.5V, J28.VCC, C2.-, U2.output_voltage, R11.pin_0, R13.pin_0, R16.pin_0, R17.pin_0, R22.pin_0, R23.pin_0, R24.pin_0, R25.pin_0, R26.Pin_1, R27.Pin_1, R28.pin_0, R29.pin_0
  VDD: PIR1.VDD, J29.VCC
  N31: J28.GND, R30.Pin_0
  VDD_2: PIR2.VDD, J30.VCC
  N32: J29.GND, R31.Pin_0
  VDD_3: PIR3.VDD, J31.VCC
  N33: J30.GND, R32.Pin_0
  VDD_4: PIR4.VDD, PIR7.VDD
  N34: J31.GND, R34.Pin_0
  VDD_5: PIR5.VDD, J33.VCC
  VCC: J32.VCC, J35.VCC
  N35: J32.GND, R35.Pin_0
  VDD_6: PIR6.VDD, J34.VCC
  N36: J33.GND, R33.Pin_0
  N37: J34.GND, R37.Pin_0
  VDD_7: PIR8.VDD, J36.VCC
  N38: J35.GND, R40.Pin_0
  VDD_8: PIR9.VDD, PIR10.VDD
  N39: J36.GND, R38.Pin_0
  N40: PIR10.GND, R36.Pin_0
  N41: BUTTON1.no_name_yet#1, VCC1.+
  N42: BUTTON1.no_name_yet#4, U2.input_voltage, C3.c-3.3µF

custom parts:
  24 NeoPixel Ring: 24 ultra bright smart LED NeoPixels are arranged in a circle with 2.6" (66mm) outer diameter. The rings are 'chainable' - connect the output pin of one to the input pin of another. Use only one microcontroller pin to control as many as you can chain together! Each LED is addressable as the driver chip is inside the LED. Each one has ~18mA constant current drive so the color will be very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
  Generic male header - 4 pins: Generic male header
  Generic male header - 2 pins: Generic male header
  Generic male header - 3 pins: Generic male header
  Waterproof Pushbutton (green): Waterproof Illuminated Pushbutton (green)
  Electrolytic Capacitor: A smd electrolytic capacitor.
